# Fritzing sketch Quick_Sketch (saved by Fritzing 0.8.7b)

parts:
  J1 = Basic Servo
  J2 = Basic Servo
  J3 = Basic Servo
  J4 = Basic Servo
  Part1 = Arduino Uno (Rev3)
  U1 = SWITCH_SPDT [package=kps-1290]
  U2 = SWITCH_SPDT [package=kps-1290]
  R1 = Rotary Potentiometer (Small) [maximum_resistance=100kΩ package=THT]
  U3 = TEMPERATURE-SENSOR [package=to-92]
  U4 = TEMPERATURE-SENSOR [package=to-92]
  U5 = TMP36 [package=to-92]
  U6 = LCD-16X2 [package=lcd-16x2]

nets:
  N1: J1.pulse, Part1.D6_PWM
  N2: J2.pulse, Part1.D7
  N3: J3.pulse, Part1.D8
  N4: J4.pulse, Part1.D9_PWM
  N5: Part1.A0, U3.ADJ
  N6: Part1.A1, U4.ADJ
  N7: Part1.A2, R1.wiper
  N8: Part1.A4/SDA, U5.VOUT, U6.K
  N9: Part1.A5/SCL, U5.GND, U6.A
  N10: Part1.GND, U1.P, U2.P
  N11: Part1.D2, U2.S
  N12: Part1.D3_PWM, U1.S

notes:
  Lidar (I2C)
  A4=SDA
  A5=SCL
  LCD (I2C)
  Same bus, A4/A5
  A0: Pressure sensor extend line
  A1: Pressure sensor retract line
  A2: Potmeter manual control (overrides serial if not null)
  Servo pins:
  6: Extend fill
  7: Extend flush
  8: Retract fill
  9: Retract flush
  Switch pins (to ground for normal run)
  2: Emergency stop
  3: Bleed (ignored if emergency off)
